// Logisim project approximate_membership.circ as structural Verilog: 3 circuits, main circuit checker
module \checker  (
  input  CLK,
  input  [31:0] key,
  input  load,
  output exists,
  output [15:0] hash,
  output [15:0] entry_0,
  output [15:0] entry_1,
  output [15:0] entry_2,
  output [15:0] entry_3,
  output [15:0] entry_4,
  output [15:0] entry_5,
  output [15:0] entry_6,
  output [15:0] entry_7,
  output [15:0] entry_8,
  output [15:0] entry_9,
  output [15:0] entry_10,
  output [15:0] entry_11,
  output [15:0] entry_12,
  output [15:0] entry_13,
  output [15:0] entry_14,
  output [15:0] entry_15
);

  wire comparator_1_eq, comparator_2_eq, comparator_3_eq, comparator_4_eq, comparator_5_eq, comparator_6_eq,
       comparator_7_eq, comparator_8_eq, comparator_9_eq, comparator_10_eq, comparator_11_eq,
       comparator_12_eq, comparator_13_eq, comparator_14_eq, comparator_15_eq, comparator_16_eq, not_1_out,
       or_1_out, or_2_out, or_3_out, or_4_out, or_5_out, or_6_out, or_7_out, or_8_out, or_9_out, or_10_out,
       or_11_out, or_12_out, or_13_out, or_14_out, or_15_out;
  wire [15:0] hashing_1_hash_0, hashing_1_hash_1, hashing_1_hash_2, hashing_1_hash_3, hashing_1_hash_4,
       hashing_1_hash_5, hashing_1_hash_6, hashing_1_hash_7, xor_1_out, xor_2_out, xor_3_out, xor_4_out,
       xor_5_out, xor_6_out;

  Comparator #(.width(16), .mode("unsigned")) comparator_1 (
    .a(entry_0), .b(hash), .eq(comparator_1_eq));  // open: gt, lt
  Comparator #(.width(16), .mode("unsigned")) comparator_2 (
    .a(entry_1), .b(hash), .eq(comparator_2_eq));  // open: gt, lt
  Comparator #(.width(16), .mode("unsigned")) comparator_3 (
    .a(entry_2), .b(hash), .eq(comparator_3_eq));  // open: gt, lt
  Comparator #(.width(16), .mode("unsigned")) comparator_4 (
    .a(entry_3), .b(hash), .eq(comparator_4_eq));  // open: gt, lt
  Comparator #(.width(16), .mode("unsigned")) comparator_5 (
    .a(entry_4), .b(hash), .eq(comparator_5_eq));  // open: gt, lt
  Comparator #(.width(16), .mode("unsigned")) comparator_6 (
    .a(entry_5), .b(hash), .eq(comparator_6_eq));  // open: gt, lt
  Comparator #(.width(16), .mode("unsigned")) comparator_7 (
    .a(entry_6), .b(hash), .eq(comparator_7_eq));  // open: gt, lt
  Comparator #(.width(16), .mode("unsigned")) comparator_8 (
    .a(entry_7), .b(hash), .eq(comparator_8_eq));  // open: gt, lt
  Comparator #(.width(16), .mode("unsigned")) comparator_9 (
    .a(entry_8), .b(hash), .eq(comparator_9_eq));  // open: gt, lt
  Comparator #(.width(16), .mode("unsigned")) comparator_10 (
    .a(entry_9), .b(hash), .eq(comparator_10_eq));  // open: gt, lt
  Comparator #(.width(16), .mode("unsigned")) comparator_11 (
    .a(entry_10), .b(hash), .eq(comparator_11_eq));  // open: gt, lt
  Comparator #(.width(16), .mode("unsigned")) comparator_12 (
    .a(entry_11), .b(hash), .eq(comparator_12_eq));  // open: gt, lt
  Comparator #(.width(16), .mode("unsigned")) comparator_13 (
    .a(entry_12), .b(hash), .eq(comparator_13_eq));  // open: gt, lt
  Comparator #(.width(16), .mode("unsigned")) comparator_14 (
    .a(entry_13), .b(hash), .eq(comparator_14_eq));  // open: gt, lt
  Comparator #(.width(16), .mode("unsigned")) comparator_15 (
    .a(entry_14), .b(hash), .eq(comparator_15_eq));  // open: gt, lt
  Comparator #(.width(16), .mode("unsigned")) comparator_16 (
    .a(entry_15), .b(hash), .eq(comparator_16_eq));  // open: gt, lt
  hashing hashing_1 (
    .block_0(key[3:0]), .block_1(key[7:4]), .block_2(key[11:8]), .block_3(key[15:12]), .block_4(key[19:16]),
    .block_5(key[23:20]), .block_6(key[27:24]), .block_7(key[31:28]), .hash_0(hashing_1_hash_0),
    .hash_1(hashing_1_hash_1), .hash_2(hashing_1_hash_2), .hash_3(hashing_1_hash_3),
    .hash_4(hashing_1_hash_4), .hash_5(hashing_1_hash_5), .hash_6(hashing_1_hash_6), .hash_7(hashing_1_hash_7));
  or or_1 (or_1_out, comparator_1_eq, comparator_2_eq);
  or or_2 (or_2_out, or_1_out, or_3_out);
  or or_3 (or_3_out, comparator_3_eq, comparator_4_eq);
  or or_4 (or_4_out, or_2_out, or_6_out);
  or or_5 (or_5_out, comparator_5_eq, comparator_6_eq);
  or or_6 (or_6_out, or_5_out, or_7_out);
  or or_7 (or_7_out, comparator_7_eq, comparator_8_eq);
  or or_8 (or_8_out, comparator_9_eq, comparator_10_eq);
  or or_9 (or_9_out, or_8_out, or_10_out);
  or or_10 (or_10_out, comparator_11_eq, comparator_12_eq);
  or or_11 (or_11_out, or_9_out, or_13_out);
  or or_12 (or_12_out, comparator_13_eq, comparator_14_eq);
  or or_13 (or_13_out, or_12_out, or_14_out);
  or or_14 (or_14_out, comparator_15_eq, comparator_16_eq);
  assign xor_1_out = hashing_1_hash_0 ^ hashing_1_hash_1;  // XOR_Gate xor_1, 16 bits wide
  assign xor_2_out = xor_1_out ^ xor_3_out;  // XOR_Gate xor_2, 16 bits wide
  assign xor_3_out = hashing_1_hash_2 ^ hashing_1_hash_3;  // XOR_Gate xor_3, 16 bits wide
  assign xor_4_out = hashing_1_hash_4 ^ hashing_1_hash_5;  // XOR_Gate xor_4, 16 bits wide
  assign xor_5_out = xor_4_out ^ xor_6_out;  // XOR_Gate xor_5, 16 bits wide
  assign xor_6_out = hashing_1_hash_6 ^ hashing_1_hash_7;  // XOR_Gate xor_6, 16 bits wide
  not not_1 (not_1_out, load);
  or or_15 (or_15_out, or_4_out, or_11_out);
  assign hash = xor_2_out ^ xor_5_out;  // XOR_Gate xor_7, 16 bits wide
  and and_1 (exists, not_1_out, or_15_out);
  CAM_16_16 cam_16_16_1 (
    .Din(hash), .load(load), .CLK(CLK), .Q_0(entry_0), .Q_1(entry_1), .Q_2(entry_2), .Q_3(entry_3),
    .Q_4(entry_4), .Q_5(entry_5), .Q_6(entry_6), .Q_7(entry_7), .Q_8(entry_8), .Q_9(entry_9),
    .Q_10(entry_10), .Q_11(entry_11), .Q_12(entry_12), .Q_13(entry_13), .Q_14(entry_14), .Q_15(entry_15));
  // Probe on hash
  // Probe on entry_0
  // Probe on entry_1
  // Probe on entry_2
  // Probe on entry_3
  // Probe on entry_4
  // Probe on entry_5
  // Probe on entry_6
  // Probe on entry_7
  // Probe on entry_8
  // Probe on entry_9
  // Probe on entry_10
  // Probe on entry_11
  // Probe on entry_12
  // Probe on entry_13
  // Probe on entry_14
  // Probe on entry_15
endmodule

module hashing (
  input  [3:0] block_0,
  input  [3:0] block_1,
  input  [3:0] block_2,
  input  [3:0] block_3,
  input  [3:0] block_4,
  input  [3:0] block_5,
  input  [3:0] block_6,
  input  [3:0] block_7,
  output [15:0] hash_0,
  output [15:0] hash_1,
  output [15:0] hash_2,
  output [15:0] hash_3,
  output [15:0] hash_4,
  output [15:0] hash_5,
  output [15:0] hash_6,
  output [15:0] hash_7
);

  ROM #(.addrWidth(4), .dataWidth(16)) rom_1 (.addr(block_0), .data(hash_0));  // open: sel
  ROM #(.addrWidth(4), .dataWidth(16)) rom_2 (.addr(block_1), .data(hash_1));  // open: sel
  ROM #(.addrWidth(4), .dataWidth(16)) rom_3 (.addr(block_2), .data(hash_2));  // open: sel
  ROM #(.addrWidth(4), .dataWidth(16)) rom_4 (.addr(block_3), .data(hash_3));  // open: sel
  ROM #(.addrWidth(4), .dataWidth(16)) rom_5 (.addr(block_4), .data(hash_4));  // open: sel
  ROM #(.addrWidth(4), .dataWidth(16)) rom_6 (.addr(block_5), .data(hash_5));  // open: sel
  ROM #(.addrWidth(4), .dataWidth(16)) rom_7 (.addr(block_6), .data(hash_6));  // open: sel
  ROM #(.addrWidth(4), .dataWidth(16)) rom_8 (.addr(block_7), .data(hash_7));  // open: sel

  // Notes on the sheet:
  //   contents of rom_1 (hex, n*v repeats v):
  //   6105 8805 961 565 9671 8563 7895 9134 9787 3992 7098 6169 5435 8434 2246 931
  //   contents of rom_2 (hex, n*v repeats v):
  //   2395 1469 4261 4151 7774 6721 3801 5823 8398 9985 1157 5907 9713 3641 4391 6434
  //   contents of rom_3 (hex, n*v repeats v):
  //   8164 8535 120 5258 2508 95 4621 7594 5368 3827 2681 1698 830 339 7348 6992
  //   contents of rom_4 (hex, n*v repeats v):
  //   855 7925 9326 3343 7552 6161 1212 9101 338 3994 5907 9447 4939 183 4585 6184
  //   contents of rom_5 (hex, n*v repeats v):
  //   6829 5732 7399 7324 9028 24 1471 5169 5098 2724 9264 2313 8762 5531 407 5949
  //   contents of rom_6 (hex, n*v repeats v):
  //   9161 9402 5694 1967 1469 5235 8841 7759 4505 9483 488 3102 5804 8174 1167 7193
  //   contents of rom_7 (hex, n*v repeats v):
  //   6929 7376 6945 195 2722 4490 7137 3670 3329 1071 9092 5096 9236 8231 6139 6273
  //   contents of rom_8 (hex, n*v repeats v):
  //   2383 3410 8702 576 5213 5032 7685 3410 1110 7656 2714 2972 5891 7535 9685 6311
endmodule

module CAM_16_16 (
  input  [15:0] Din,
  input  load,
  input  CLK,
  output [15:0] Q_0,
  output [15:0] Q_1,
  output [15:0] Q_2,
  output [15:0] Q_3,
  output [15:0] Q_4,
  output [15:0] Q_5,
  output [15:0] Q_6,
  output [15:0] Q_7,
  output [15:0] Q_8,
  output [15:0] Q_9,
  output [15:0] Q_10,
  output [15:0] Q_11,
  output [15:0] Q_12,
  output [15:0] Q_13,
  output [15:0] Q_14,
  output [15:0] Q_15
);

  Shift_Register #(.width(16), .length(16)) shift_register_1 (
    .shift(load), .in(Din), .clk(CLK), .q0(Q_0), .q1(Q_1), .q2(Q_2), .q3(Q_3), .q4(Q_4), .q5(Q_5), .q6(Q_6),
    .q7(Q_7), .q8(Q_8), .q9(Q_9), .q10(Q_10), .q11(Q_11), .q12(Q_12), .q13(Q_13), .q14(Q_14), .q15(Q_15));  // open: out, load, clr, d0, d1, d2, d3, d4, d5, d6, d7, d8, d9, d10, d11, d12, d13, d14, d15
endmodule
