// Logisim project penc.circ as structural Verilog: 13 circuits, main circuit penc_rec_4
module penc_rec_4 (
  input  [15:0] y,
  output [3:0] x,
  output valid
);

  wire or_1_out, or_2_out, or_3_out, or_4_out, or_5_out, or_6_out, or_7_out, or_8_out, or_9_out, or_10_out,
       or_11_out, or_12_out, or_13_out, or_15_out, VLN, XL0, XL1, XL2, XR0, XR1, XR2, YL0, YL1, YL2, YR0,
       YR1, YR2;

  or or_1 (or_1_out, y[0], y[1]);
  or or_2 (or_2_out, or_1_out, or_3_out);
  or or_3 (or_3_out, y[2], y[3]);
  or or_4 (or_4_out, y[4], y[5]);
  or or_5 (or_5_out, or_4_out, or_6_out);
  or or_6 (or_6_out, y[6], y[7]);
  or or_7 (or_7_out, y[8], y[9]);
  or or_8 (or_8_out, or_7_out, or_9_out);
  or or_9 (or_9_out, y[10], y[11]);
  or or_10 (or_10_out, y[12], y[13]);
  or or_11 (or_11_out, or_10_out, or_12_out);
  or or_12 (or_12_out, y[14], y[15]);
  or or_13 (or_13_out, or_2_out, or_5_out);
  or or_14 (valid, or_13_out, or_15_out);
  or or_15 (or_15_out, or_8_out, or_11_out);
  penc_rec_3 YR (.y(y[7:0]), .x({YR2, YR1, YR0}));  // open: valid
  penc_rec_3 YL (.y(y[15:8]), .x({YL2, YL1, YL0}), .valid(x[3]));
  not not_1 (VLN, x[3]);
  and and_1 (XR0, YR0, VLN);
  and and_2 (XR1, YR1, VLN);
  and and_3 (XR2, YR2, VLN);
  and and_4 (XL0, YL0, x[3]);
  and and_5 (XL1, YL1, x[3]);
  and and_6 (XL2, YL2, x[3]);
  or or_16 (x[0], XR0, XL0);
  or or_17 (x[1], XR1, XL1);
  or or_18 (x[2], XR2, XL2);

  // Other names for the same wires on the sheet: VL = x[3]
endmodule

module penc_rec_3 (
  input  [7:0] y,
  output [2:0] x,
  output valid
);

  wire and_1_out, and_2_out, and_3_out, and_4_out, not_1_out, or_1_out, or_2_out, or_3_out, or_4_out,
       or_5_out, or_6_out;
  wire [1:0] YL_x, YR_x;

  or or_1 (or_1_out, y[0], y[1]);
  or or_2 (or_2_out, y[2], y[3]);
  or or_3 (or_3_out, y[4], y[5]);
  or or_4 (or_4_out, y[6], y[7]);
  penc_rec_2 YR (.y(y[3:0]), .x(YR_x));  // open: valid
  not not_1 (not_1_out, x[2]);
  penc_rec_2 YL (.y(y[7:4]), .x(YL_x), .valid(x[2]));
  or or_5 (or_5_out, or_1_out, or_2_out);
  or or_6 (or_6_out, or_3_out, or_4_out);
  or or_7 (valid, or_5_out, or_6_out);
  and and_1 (and_1_out, YR_x[0], not_1_out);
  and and_2 (and_2_out, YR_x[1], not_1_out);
  and and_3 (and_3_out, YL_x[0], x[2]);
  and and_4 (and_4_out, YL_x[1], x[2]);
  or or_8 (x[0], and_1_out, and_3_out);
  or or_9 (x[1], and_2_out, and_4_out);
endmodule

module penc_rec_2 (
  input  [3:0] y,
  output [1:0] x,
  output valid
);

  wire and_1_out, and_2_out, not_1_out, or_1_out, or_2_out, penc_rec_1_1_x, penc_rec_1_2_x;

  or or_1 (or_1_out, y[0], y[1]);
  or or_2 (or_2_out, y[2], y[3]);
  or or_3 (valid, or_1_out, or_2_out);
  penc_rec_1 penc_rec_1_1 (.y(y[1:0]), .x(penc_rec_1_1_x));  // open: valid
  penc_rec_1 penc_rec_1_2 (.y(y[3:2]), .x(penc_rec_1_2_x), .valid(x[1]));
  not not_1 (not_1_out, x[1]);
  and and_1 (and_1_out, penc_rec_1_1_x, not_1_out);
  and and_2 (and_2_out, penc_rec_1_2_x, x[1]);
  or or_4 (x[0], and_1_out, and_2_out);

  // Other names for the same wires on the sheet: yL[1:0] = y[3:2]; yR[1:0] = y[1:0]

  // Notes on the sheet:
  //   x
  //   x
endmodule

module penc_rec_1 (
  input  [1:0] y,
  output x,
  output valid
);

  or or_1 (valid, y[0], y[1]);

  assign x = y[1];

  // Other names for the same wires on the sheet: yo = y[0]
endmodule

module penc_nonrec_4 (
  input  [15:0] y,
  output [3:0] x,
  output valid
);

  wire or_1_out, or_2_out, or_3_out, or_4_out, or_5_out, or_6_out, or_7_out, or_8_out, or_9_out, or_10_out,
       or_11_out, or_12_out, or_13_out, or_14_out, x_enc_0, x_enc_1, x_enc_2, x_enc_3, x_enc_4, x_enc_5,
       x_enc_6, x_enc_7, x_enc_8, x_enc_9, x_enc_10, x_enc_11, x_enc_12, x_enc_13, x_enc_14, x_enc_15,
       xor_1_out, xor_2_out, xor_3_out, xor_4_out, xor_5_out, xor_6_out, xor_7_out, xor_8_out, xor_9_out,
       xor_10_out, xor_11_out, xor_12_out, xor_13_out, xor_14_out, xor_15_out, y_eff_0, y_eff_1, y_eff_2,
       y_eff_3, y_eff_4, y_eff_5, y_eff_6, y_eff_7, y_eff_8, y_eff_9, y_eff_10, y_eff_11, y_eff_12, y_eff_13,
       y_eff_14, y_eff_15, y_eff_N_0, y_eff_N_1, y_eff_N_2, y_eff_N_3, y_eff_N_4, y_eff_N_5, y_eff_N_6,
       y_eff_N_7, y_eff_N_8, y_eff_N_9, y_eff_N_10, y_eff_N_11, y_eff_N_12, y_eff_N_13, y_eff_N_14,
       y_eff_N_15;
  wire [15:0] eff_N_q;

  Multiplexer #(.enable("false")) multiplexer_1 (.in0(y_eff_N_15), .in1(y_eff_15), .out(x_enc_15), .sel(1'b1));
  xor xor_1 (xor_1_out, 1'b1, x_enc_15);
  Multiplexer #(.enable("false")) multiplexer_2 (.in0(y_eff_N_14), .in1(y_eff_14), .out(x_enc_14), .sel(xor_1_out));
  or or_1 (or_1_out, y[0], y[1]);
  or or_2 (or_2_out, or_1_out, or_3_out);
  or or_3 (or_3_out, y[2], y[3]);
  or or_4 (or_4_out, or_2_out, or_6_out);
  or or_5 (or_5_out, y[4], y[5]);
  or or_6 (or_6_out, or_5_out, or_7_out);
  or or_7 (or_7_out, y[6], y[7]);
  or or_8 (or_8_out, y[8], y[9]);
  or or_9 (or_9_out, or_8_out, or_10_out);
  or or_10 (or_10_out, y[10], y[11]);
  or or_11 (or_11_out, or_9_out, or_13_out);
  or or_12 (or_12_out, y[12], y[13]);
  or or_13 (or_13_out, or_12_out, or_14_out);
  or or_14 (or_14_out, y[14], y[15]);
  xor xor_2 (xor_2_out, xor_1_out, x_enc_14);
  or or_15 (valid, or_4_out, or_11_out);
  Multiplexer #(.enable("false")) multiplexer_3 (.in0(y_eff_N_13), .in1(y_eff_13), .out(x_enc_13), .sel(xor_2_out));
  xor xor_3 (xor_3_out, xor_2_out, x_enc_13);
  Multiplexer #(.enable("false")) multiplexer_4 (.in0(y_eff_N_12), .in1(y_eff_12), .out(x_enc_12), .sel(xor_3_out));
  eff_or_16 eff (
    .p(y),
    .q({y_eff_15, y_eff_14, y_eff_13, y_eff_12, y_eff_11, y_eff_10, y_eff_9, y_eff_8, y_eff_7, y_eff_6, y_eff_5, y_eff_4, y_eff_3, y_eff_2, y_eff_1, y_eff_0}));
  Multiplexer #(.enable("false")) multiplexer_5 (.in0(y_eff_N_11), .in1(y_eff_11), .out(x_enc_11), .sel(xor_4_out));
  xor xor_4 (xor_4_out, xor_3_out, x_enc_12);
  xor xor_5 (xor_5_out, xor_4_out, x_enc_11);
  Multiplexer #(.enable("false")) multiplexer_6 (.in0(y_eff_N_10), .in1(y_eff_10), .out(x_enc_10), .sel(xor_5_out));
  xor xor_6 (xor_6_out, xor_5_out, x_enc_10);
  eff_or_16 eff_N (.p(y), .q(eff_N_q));
  Multiplexer #(.enable("false")) multiplexer_7 (.in0(y_eff_N_9), .in1(y_eff_9), .out(x_enc_9), .sel(xor_6_out));
  not not_1 (y_eff_N_0, eff_N_q[0]);
  not not_2 (y_eff_N_1, eff_N_q[1]);
  not not_3 (y_eff_N_2, eff_N_q[2]);
  not not_4 (y_eff_N_3, eff_N_q[3]);
  not not_5 (y_eff_N_4, eff_N_q[4]);
  not not_6 (y_eff_N_5, eff_N_q[5]);
  not not_7 (y_eff_N_6, eff_N_q[6]);
  not not_8 (y_eff_N_7, eff_N_q[7]);
  not not_9 (y_eff_N_8, eff_N_q[8]);
  not not_10 (y_eff_N_9, eff_N_q[9]);
  not not_11 (y_eff_N_10, eff_N_q[10]);
  not not_12 (y_eff_N_11, eff_N_q[11]);
  not not_13 (y_eff_N_12, eff_N_q[12]);
  not not_14 (y_eff_N_13, eff_N_q[13]);
  not not_15 (y_eff_N_14, eff_N_q[14]);
  not not_16 (y_eff_N_15, eff_N_q[15]);
  Multiplexer #(.enable("false")) multiplexer_8 (.in0(y_eff_N_8), .in1(y_eff_8), .out(x_enc_8), .sel(xor_7_out));
  xor xor_7 (xor_7_out, xor_6_out, x_enc_9);
  xor xor_8 (xor_8_out, xor_7_out, x_enc_8);
  enc_rec_4 enc_rec_4_1 (
    .y({x_enc_15, x_enc_14, x_enc_13, x_enc_12, x_enc_11, x_enc_10, x_enc_9, x_enc_8, x_enc_7, x_enc_6, x_enc_5, x_enc_4, x_enc_3, x_enc_2, x_enc_1, x_enc_0}),
    .x(x));
  Multiplexer #(.enable("false")) multiplexer_9 (.in0(y_eff_N_7), .in1(y_eff_7), .out(x_enc_7), .sel(xor_8_out));
  xor xor_9 (xor_9_out, xor_8_out, x_enc_7);
  Multiplexer #(.enable("false")) multiplexer_10 (.in0(y_eff_N_6), .in1(y_eff_6), .out(x_enc_6), .sel(xor_9_out));
  xor xor_10 (xor_10_out, xor_9_out, x_enc_6);
  Multiplexer #(.enable("false")) multiplexer_11 (.in0(y_eff_N_5), .in1(y_eff_5), .out(x_enc_5), .sel(xor_10_out));
  xor xor_11 (xor_11_out, xor_10_out, x_enc_5);
  Multiplexer #(.enable("false")) multiplexer_12 (.in0(y_eff_N_4), .in1(y_eff_4), .out(x_enc_4), .sel(xor_11_out));
  Multiplexer #(.enable("false")) multiplexer_13 (.in0(y_eff_N_3), .in1(y_eff_3), .out(x_enc_3), .sel(xor_12_out));
  xor xor_12 (xor_12_out, xor_11_out, x_enc_4);
  Multiplexer #(.enable("false")) multiplexer_14 (.in0(y_eff_N_2), .in1(y_eff_2), .out(x_enc_2), .sel(xor_13_out));
  xor xor_13 (xor_13_out, xor_12_out, x_enc_3);
  xor xor_14 (xor_14_out, xor_13_out, x_enc_2);
  Multiplexer #(.enable("false")) multiplexer_15 (.in0(y_eff_N_1), .in1(y_eff_1), .out(x_enc_1), .sel(xor_14_out));
  Multiplexer #(.enable("false")) multiplexer_16 (.in0(y_eff_N_0), .in1(y_eff_0), .out(x_enc_0), .sel(xor_15_out));
  xor xor_15 (xor_15_out, xor_14_out, x_enc_1);
endmodule

module eff_or_16 (
  input  [15:0] p,
  output [15:0] q
);

  wire [7:0] eff_or_8_1_q;

  eff_or_8 eff_or_8_1 (.p(p[7:0]), .q(eff_or_8_1_q));
  eff_or_8 eff_or_8_2 (.p(p[15:8]), .q(q[15:8]));
  or or_1 (q[6], eff_or_8_1_q[6], q[7]);
  or or_2 (q[7], eff_or_8_1_q[7], q[8]);
  or or_3 (q[5], eff_or_8_1_q[5], q[6]);
  or or_4 (q[3], eff_or_8_1_q[3], q[4]);
  or or_5 (q[4], eff_or_8_1_q[4], q[5]);
  or or_6 (q[1], eff_or_8_1_q[1], q[2]);
  or or_7 (q[2], eff_or_8_1_q[2], q[3]);
  or or_8 (q[0], eff_or_8_1_q[0], q[1]);
endmodule

module eff_or_8 (
  input  [7:0] p,
  output [7:0] q
);

  wire [3:0] eff_or_4_1_q;

  eff_or_4 eff_or_4_1 (.p(p[3:0]), .q(eff_or_4_1_q));
  eff_or_4 eff_or_4_2 (.p(p[7:4]), .q(q[7:4]));
  or or_1 (q[3], eff_or_4_1_q[3], q[4]);
  or or_2 (q[1], eff_or_4_1_q[1], q[2]);
  or or_3 (q[2], eff_or_4_1_q[2], q[3]);
  or or_4 (q[0], eff_or_4_1_q[0], q[1]);
endmodule

module eff_or_4 (
  input  [3:0] p,
  output [3:0] q
);

  wire [1:0] eff_or_2_1_q;

  eff_or_2 eff_or_2_1 (.p(p[1:0]), .q(eff_or_2_1_q));
  or or_1 (q[1], eff_or_2_1_q[1], q[2]);
  eff_or_2 eff_or_2_2 (.p(p[3:2]), .q(q[3:2]));
  or or_2 (q[0], eff_or_2_1_q[0], q[1]);
endmodule

module eff_or_2 (
  input  [1:0] p,
  output [1:0] q
);

  or or_1 (q[0], p[0], p[1]);

  assign q[1] = p[1];

  // Other names for the same wires on the sheet: q1 = p[1]
endmodule

module enc_rec_1 (
  input  [1:0] y,
  output x
);


  assign x = y[1];
endmodule

module enc_rec_2 (
  input  [3:0] y,
  output [1:0] x
);

  wire [1:0] or_1_out;

  or or_1 (or_1_out[0], y[0], y[2]);
  or or_2 (or_1_out[1], y[1], y[3]);
  or or_3 (x[1], y[2], y[3]);
  enc_rec_1 enc_rec_1_1 (.y(or_1_out), .x(x[0]));
endmodule

module enc_rec_3 (
  input  [7:0] y,
  output [2:0] x
);

  wire or_5_out, or_6_out;
  wire [3:0] or_1_out;

  or or_1 (or_1_out[0], y[0], y[4]);
  or or_2 (or_1_out[1], y[1], y[5]);
  or or_3 (or_1_out[2], y[2], y[6]);
  or or_4 (or_1_out[3], y[3], y[7]);
  or or_5 (or_5_out, y[4], y[5]);
  or or_6 (or_6_out, y[6], y[7]);
  enc_rec_2 enc_rec_2_1 (.y(or_1_out), .x(x[1:0]));
  or or_7 (x[2], or_5_out, or_6_out);
endmodule

module enc_rec_4 (
  input  [15:0] y,
  output [3:0] x
);

  wire or_9_out, or_10_out, or_11_out, or_12_out, or_13_out, or_15_out;
  wire [7:0] or_1_out;

  or or_1 (or_1_out[0], y[0], y[8]);
  or or_2 (or_1_out[1], y[1], y[9]);
  or or_3 (or_1_out[2], y[2], y[10]);
  or or_4 (or_1_out[3], y[3], y[11]);
  or or_5 (or_1_out[4], y[4], y[12]);
  or or_6 (or_1_out[5], y[5], y[13]);
  or or_7 (or_1_out[6], y[6], y[14]);
  or or_8 (or_1_out[7], y[7], y[15]);
  enc_rec_3 enc_rec_3_1 (.y(or_1_out), .x(x[2:0]));
  or or_9 (or_9_out, y[8], y[9]);
  or or_10 (or_10_out, y[10], y[11]);
  or or_11 (or_11_out, y[12], y[13]);
  or or_12 (or_12_out, y[14], y[15]);
  or or_13 (or_13_out, or_9_out, or_10_out);
  or or_14 (x[3], or_13_out, or_15_out);
  or or_15 (or_15_out, or_11_out, or_12_out);
endmodule
