// Logisim project pocket_dict.circ as structural Verilog: 6 circuits, main circuit pocket_dict
module pocket_dict (
  input  [7:0] X,
  input  CLK,
  input  op,
  output exists,
  output [23:0] header,
  output [4:0] body_entry_15,
  output [4:0] body_entry_14,
  output [4:0] body_entry_13,
  output [4:0] body_entry_12,
  output [4:0] body_entry_11,
  output [4:0] body_entry_10,
  output [4:0] body_entry_9,
  output [4:0] body_entry_8,
  output [4:0] body_entry_7,
  output [4:0] body_entry_6,
  output [4:0] body_entry_5,
  output [4:0] body_entry_4,
  output [4:0] body_entry_3,
  output [4:0] body_entry_2,
  output [4:0] body_entry_1,
  output [4:0] body_entry_0
);

  wire and_1_out, and_2_out, and_3_out, and_4_out, and_5_out, and_6_out, and_7_out, and_8_out, and_9_out,
       and_10_out, and_11_out, and_12_out, and_13_out, and_14_out, and_15_out, and_16_out, comparator_25_eq,
       comparator_26_eq, comparator_27_eq, comparator_28_eq, comparator_29_eq, comparator_30_eq,
       comparator_31_eq, comparator_32_eq, comparator_33_eq, comparator_34_eq, comparator_35_eq,
       comparator_36_eq, comparator_37_eq, comparator_38_eq, comparator_39_eq, comparator_40_eq, or_1_out,
       or_2_out, or_3_out, or_4_out, or_5_out, or_6_out, or_7_out, or_8_out, or_9_out, or_10_out, or_11_out,
       or_12_out, or_13_out, or_15_out;
  wire [4:0] adder_1_out, body_entry_0_masked, body_entry_0_t, body_entry_1_masked, body_entry_1_t,
       body_entry_2_masked, body_entry_2_t, body_entry_3_masked, body_entry_3_t, body_entry_4_masked,
       body_entry_4_t, body_entry_5_masked, body_entry_5_t, body_entry_6_masked, body_entry_6_t,
       body_entry_7_masked, body_entry_7_t, body_entry_8_masked, body_entry_8_t, body_entry_9_masked,
       body_entry_9_t, body_entry_10_masked, body_entry_10_t, body_entry_11_masked, body_entry_11_t,
       body_entry_12_masked, body_entry_12_t, body_entry_13_masked, body_entry_13_t, body_entry_14_masked,
       body_entry_14_t, body_entry_15_masked, body_entry_15_t, q_5bits, S_0, S_1, S_2, S_3, S_4, S_5, S_6,
       S_7, S_8, S_9, S_10, S_11, S_12, S_13, S_14, S_15, S_16, S_17, S_18, S_19, S_20, S_21, S_22, S_23,
       shift_treshold_body, shift_treshold_header;
  wire [7:0] shifter_1_out;
  wire [15:0] bmask, body_col_0, body_col_1, body_col_2, body_col_3, body_col_4;
  wire [23:0] hmask, hmask_op_1, is_req_block, not_1_out;
  wire [31:0] bit_extender_2_out;

  assign not_1_out = ~header;  // NOT_Gate not_1, 24 bits wide
  Comparator #(.width(5)) comparator_1 (.a(S_0), .b(q_5bits), .eq(is_req_block[0]));  // open: gt, lt
  Comparator #(.width(5)) comparator_2 (.a(S_1), .b(q_5bits), .eq(is_req_block[1]));  // open: gt, lt
  Comparator #(.width(5)) comparator_3 (.a(S_2), .b(q_5bits), .eq(is_req_block[2]));  // open: gt, lt
  Comparator #(.width(5)) comparator_4 (.a(S_3), .b(q_5bits), .eq(is_req_block[3]));  // open: gt, lt
  Comparator #(.width(5)) comparator_5 (.a(S_4), .b(q_5bits), .eq(is_req_block[4]));  // open: gt, lt
  Comparator #(.width(5)) comparator_6 (.a(S_5), .b(q_5bits), .eq(is_req_block[5]));  // open: gt, lt
  Comparator #(.width(5)) comparator_7 (.a(S_6), .b(q_5bits), .eq(is_req_block[6]));  // open: gt, lt
  Comparator #(.width(5)) comparator_8 (.a(S_7), .b(q_5bits), .eq(is_req_block[7]));  // open: gt, lt
  Comparator #(.width(5)) comparator_9 (.a(S_8), .b(q_5bits), .eq(is_req_block[8]));  // open: gt, lt
  Comparator #(.width(5)) comparator_10 (.a(S_9), .b(q_5bits), .eq(is_req_block[9]));  // open: gt, lt
  Comparator #(.width(5)) comparator_11 (.a(S_10), .b(q_5bits), .eq(is_req_block[10]));  // open: gt, lt
  Comparator #(.width(5)) comparator_12 (.a(S_11), .b(q_5bits), .eq(is_req_block[11]));  // open: gt, lt
  Comparator #(.width(5)) comparator_13 (.a(S_12), .b(q_5bits), .eq(is_req_block[12]));  // open: gt, lt
  Comparator #(.width(5)) comparator_14 (.a(S_13), .b(q_5bits), .eq(is_req_block[13]));  // open: gt, lt
  Comparator #(.width(5)) comparator_15 (.a(S_14), .b(q_5bits), .eq(is_req_block[14]));  // open: gt, lt
  Comparator #(.width(5)) comparator_16 (.a(S_15), .b(q_5bits), .eq(is_req_block[15]));  // open: gt, lt
  Comparator #(.width(5)) comparator_17 (.a(S_16), .b(q_5bits), .eq(is_req_block[16]));  // open: gt, lt
  Comparator #(.width(5)) comparator_18 (.a(S_17), .b(q_5bits), .eq(is_req_block[17]));  // open: gt, lt
  Comparator #(.width(5)) comparator_19 (.a(S_18), .b(q_5bits), .eq(is_req_block[18]));  // open: gt, lt
  Comparator #(.width(5)) comparator_20 (.a(S_19), .b(q_5bits), .eq(is_req_block[19]));  // open: gt, lt
  Comparator #(.width(5)) comparator_21 (.a(S_20), .b(q_5bits), .eq(is_req_block[20]));  // open: gt, lt
  Comparator #(.width(5)) comparator_22 (.a(S_21), .b(q_5bits), .eq(is_req_block[21]));  // open: gt, lt
  Comparator #(.width(5)) comparator_23 (.a(S_22), .b(q_5bits), .eq(is_req_block[22]));  // open: gt, lt
  Comparator #(.width(5)) comparator_24 (.a(S_23), .b(q_5bits), .eq(is_req_block[23]));  // open: gt, lt
  ppc_sum_24 ppc_sum_24_1 (
    .x(not_1_out), .y_23(S_23), .y_22(S_22), .y_21(S_21), .y_20(S_20), .y_19(S_19), .y_18(S_18), .y_17(S_17),
    .y_16(S_16), .y_15(S_15), .y_14(S_14), .y_13(S_13), .y_12(S_12), .y_11(S_11), .y_10(S_10), .y_9(S_9),
    .y_8(S_8), .y_7(S_7), .y_6(S_6), .y_5(S_5), .y_4(S_4), .y_3(S_3), .y_2(S_2), .y_1(S_1), .y_0(S_0));
  Comparator #(.width(5)) comparator_25 (.a(X[4:0]), .b(body_entry_0_masked), .eq(comparator_25_eq));  // open: gt, lt
  Comparator #(.width(5)) comparator_26 (.a(X[4:0]), .b(body_entry_1_masked), .eq(comparator_26_eq));  // open: gt, lt
  Comparator #(.width(5)) comparator_27 (.a(X[4:0]), .b(body_entry_2_masked), .eq(comparator_27_eq));  // open: gt, lt
  Comparator #(.width(5)) comparator_28 (.a(X[4:0]), .b(body_entry_3_masked), .eq(comparator_28_eq));  // open: gt, lt
  Comparator #(.width(5)) comparator_29 (.a(X[4:0]), .b(body_entry_4_masked), .eq(comparator_29_eq));  // open: gt, lt
  Comparator #(.width(5)) comparator_30 (.a(X[4:0]), .b(body_entry_5_masked), .eq(comparator_30_eq));  // open: gt, lt
  Comparator #(.width(5)) comparator_31 (.a(X[4:0]), .b(body_entry_6_masked), .eq(comparator_31_eq));  // open: gt, lt
  Comparator #(.width(5)) comparator_32 (.a(X[4:0]), .b(body_entry_7_masked), .eq(comparator_32_eq));  // open: gt, lt
  Comparator #(.width(5)) comparator_33 (.a(X[4:0]), .b(body_entry_8_masked), .eq(comparator_33_eq));  // open: gt, lt
  Comparator #(.width(5)) comparator_34 (.a(X[4:0]), .b(body_entry_9_masked), .eq(comparator_34_eq));  // open: gt, lt
  Comparator #(.width(5)) comparator_35 (.a(X[4:0]), .b(body_entry_10_masked), .eq(comparator_35_eq));  // open: gt, lt
  Comparator #(.width(5)) comparator_36 (.a(X[4:0]), .b(body_entry_11_masked), .eq(comparator_36_eq));  // open: gt, lt
  Comparator #(.width(5)) comparator_37 (.a(X[4:0]), .b(body_entry_12_masked), .eq(comparator_37_eq));  // open: gt, lt
  Comparator #(.width(5)) comparator_38 (.a(X[4:0]), .b(body_entry_13_masked), .eq(comparator_38_eq));  // open: gt, lt
  Comparator #(.width(5)) comparator_39 (.a(X[4:0]), .b(body_entry_14_masked), .eq(comparator_39_eq));  // open: gt, lt
  Comparator #(.width(5)) comparator_40 (.a(X[4:0]), .b(body_entry_15_masked), .eq(comparator_40_eq));  // open: gt, lt
  and and_1 (and_1_out, bmask[0], comparator_25_eq);
  and and_2 (and_2_out, bmask[1], comparator_26_eq);
  and and_3 (and_3_out, bmask[2], comparator_27_eq);
  and and_4 (and_4_out, bmask[3], comparator_28_eq);
  and and_5 (and_5_out, bmask[4], comparator_29_eq);
  and and_6 (and_6_out, bmask[5], comparator_30_eq);
  and and_7 (and_7_out, bmask[6], comparator_31_eq);
  and and_8 (and_8_out, bmask[7], comparator_32_eq);
  and and_9 (and_9_out, bmask[8], comparator_33_eq);
  and and_10 (and_10_out, bmask[9], comparator_34_eq);
  and and_11 (and_11_out, bmask[10], comparator_35_eq);
  and and_12 (and_12_out, bmask[11], comparator_36_eq);
  and and_13 (and_13_out, bmask[12], comparator_37_eq);
  and and_14 (and_14_out, bmask[13], comparator_38_eq);
  and and_15 (and_15_out, bmask[14], comparator_39_eq);
  and and_16 (and_16_out, bmask[15], comparator_40_eq);
  or or_1 (or_1_out, and_1_out, and_2_out);
  or or_2 (or_2_out, or_1_out, or_3_out);
  or or_3 (or_3_out, and_3_out, and_4_out);
  or or_4 (or_4_out, and_5_out, and_6_out);
  or or_5 (or_5_out, or_4_out, or_6_out);
  or or_6 (or_6_out, and_7_out, and_8_out);
  or or_7 (or_7_out, and_9_out, and_10_out);
  or or_8 (or_8_out, or_7_out, or_9_out);
  or or_9 (or_9_out, and_11_out, and_12_out);
  or or_10 (or_10_out, and_13_out, and_14_out);
  or or_11 (or_11_out, or_10_out, or_12_out);
  or or_12 (or_12_out, and_15_out, and_16_out);
  or or_13 (or_13_out, or_2_out, or_5_out);
  or or_14 (exists, or_13_out, or_15_out);
  or or_15 (or_15_out, or_8_out, or_11_out);
  MSR_24 msr_24_1 (.Din(1'b1), .op(op), .shift_threshold(shift_treshold_header), .CLK(CLK), .contents(header));
  assign q_5bits = {{2{1'b0}}, X[7:5]};  // Bit_Extender bit_extender_1
  Adder #(.width(5)) adder_1 (.a(shift_treshold_header), .b(q_5bits), .out(adder_1_out));  // open: cin, cout
  assign bit_extender_2_out = {{8{1'b0}}, is_req_block};  // Bit_Extender bit_extender_2
  Multiplexer #(.width(24), .enable("false")) multiplexer_1 (
    .in0(is_req_block), .in1(hmask_op_1), .out(hmask), .sel(op));
  assign hmask_op_1 = is_req_block & header;  // AND_Gate and_17, 24 bits wide
  Shifter #(.width(24)) shifter_1 (.in(hmask), .\dist (q_5bits), .out({bmask, shifter_1_out}));
  Subtractor #(.width(5)) subtractor_1 (.a(adder_1_out), .b(5'b01000), .out(shift_treshold_body));  // open: bin, bout
  transpose_16_5 transpose_16_5_1 (
    .x0(body_col_0), .x1(body_col_1), .x2(body_col_2), .x3(body_col_3), .x4(body_col_4), .y15(body_entry_15),
    .y14(body_entry_14), .y13(body_entry_13), .y12(body_entry_12), .y11(body_entry_11), .y10(body_entry_10),
    .y9(body_entry_9), .y8(body_entry_8), .y7(body_entry_7), .y6(body_entry_6), .y5(body_entry_5),
    .y4(body_entry_4), .y3(body_entry_3), .y2(body_entry_2), .y1(body_entry_1), .y0(body_entry_0));
  Priority_Encoder #(.select(5)) priority_encoder_1 (
    .in0(bit_extender_2_out[0]), .in1(bit_extender_2_out[1]), .in2(bit_extender_2_out[2]),
    .in3(bit_extender_2_out[3]), .in4(bit_extender_2_out[4]), .in5(bit_extender_2_out[5]),
    .in6(bit_extender_2_out[6]), .in7(bit_extender_2_out[7]), .in8(bit_extender_2_out[8]),
    .in9(bit_extender_2_out[9]), .in10(bit_extender_2_out[10]), .in11(bit_extender_2_out[11]),
    .in12(bit_extender_2_out[12]), .in13(bit_extender_2_out[13]), .in14(bit_extender_2_out[14]),
    .in15(bit_extender_2_out[15]), .in16(bit_extender_2_out[16]), .in17(bit_extender_2_out[17]),
    .in18(bit_extender_2_out[18]), .in19(bit_extender_2_out[19]), .in20(bit_extender_2_out[20]),
    .in21(bit_extender_2_out[21]), .in22(bit_extender_2_out[22]), .in23(bit_extender_2_out[23]),
    .in24(bit_extender_2_out[24]), .in25(bit_extender_2_out[25]), .in26(bit_extender_2_out[26]),
    .in27(bit_extender_2_out[27]), .in28(bit_extender_2_out[28]), .in29(bit_extender_2_out[29]),
    .in30(bit_extender_2_out[30]), .in31(bit_extender_2_out[31]), .out(shift_treshold_header));  // open: gs, en_out, en_in
  MSR_16 msr_16_1 (.Din(X[0]), .op(op), .shift_threshold(shift_treshold_body), .CLK(CLK), .contents(body_col_0));
  MSR_16 msr_16_2 (.Din(X[1]), .op(op), .shift_threshold(shift_treshold_body), .CLK(CLK), .contents(body_col_1));
  MSR_16 msr_16_3 (.Din(X[2]), .op(op), .shift_threshold(shift_treshold_body), .CLK(CLK), .contents(body_col_2));
  transpose_16_5 transpose_16_5_2 (
    .x0(body_col_0), .x1(body_col_1), .x2(body_col_2), .x3(body_col_3), .x4(body_col_4),
    .y15(body_entry_15_t), .y14(body_entry_14_t), .y13(body_entry_13_t), .y12(body_entry_12_t),
    .y11(body_entry_11_t), .y10(body_entry_10_t), .y9(body_entry_9_t), .y8(body_entry_8_t),
    .y7(body_entry_7_t), .y6(body_entry_6_t), .y5(body_entry_5_t), .y4(body_entry_4_t), .y3(body_entry_3_t),
    .y2(body_entry_2_t), .y1(body_entry_1_t), .y0(body_entry_0_t));
  MSR_16 msr_16_4 (.Din(X[3]), .op(op), .shift_threshold(shift_treshold_body), .CLK(CLK), .contents(body_col_3));
  MSR_16 msr_16_5 (.Din(X[4]), .op(op), .shift_threshold(shift_treshold_body), .CLK(CLK), .contents(body_col_4));
  Multiplexer #(.width(5), .enable("false")) multiplexer_2 (
    .in0({5{1'b0}}), .in1(body_entry_15_t), .out(body_entry_15_masked), .sel(bmask[15]));
  Multiplexer #(.width(5), .enable("false")) multiplexer_3 (
    .in0({5{1'b0}}), .in1(body_entry_14_t), .out(body_entry_14_masked), .sel(bmask[14]));
  Multiplexer #(.width(5), .enable("false")) multiplexer_4 (
    .in0({5{1'b0}}), .in1(body_entry_13_t), .out(body_entry_13_masked), .sel(bmask[13]));
  Multiplexer #(.width(5), .enable("false")) multiplexer_5 (
    .in0({5{1'b0}}), .in1(body_entry_12_t), .out(body_entry_12_masked), .sel(bmask[12]));
  Multiplexer #(.width(5), .enable("false")) multiplexer_6 (
    .in0({5{1'b0}}), .in1(body_entry_11_t), .out(body_entry_11_masked), .sel(bmask[11]));
  Multiplexer #(.width(5), .enable("false")) multiplexer_7 (
    .in0({5{1'b0}}), .in1(body_entry_10_t), .out(body_entry_10_masked), .sel(bmask[10]));
  Multiplexer #(.width(5), .enable("false")) multiplexer_8 (
    .in0({5{1'b0}}), .in1(body_entry_9_t), .out(body_entry_9_masked), .sel(bmask[9]));
  Multiplexer #(.width(5), .enable("false")) multiplexer_9 (
    .in0({5{1'b0}}), .in1(body_entry_8_t), .out(body_entry_8_masked), .sel(bmask[8]));
  Multiplexer #(.width(5), .enable("false")) multiplexer_10 (
    .in0({5{1'b0}}), .in1(body_entry_7_t), .out(body_entry_7_masked), .sel(bmask[7]));
  Multiplexer #(.width(5), .enable("false")) multiplexer_11 (
    .in0({5{1'b0}}), .in1(body_entry_6_t), .out(body_entry_6_masked), .sel(bmask[6]));
  Multiplexer #(.width(5), .enable("false")) multiplexer_12 (
    .in0({5{1'b0}}), .in1(body_entry_5_t), .out(body_entry_5_masked), .sel(bmask[5]));
  Multiplexer #(.width(5), .enable("false")) multiplexer_13 (
    .in0({5{1'b0}}), .in1(body_entry_4_t), .out(body_entry_4_masked), .sel(bmask[4]));
  Multiplexer #(.width(5), .enable("false")) multiplexer_14 (
    .in0({5{1'b0}}), .in1(body_entry_3_t), .out(body_entry_3_masked), .sel(bmask[3]));
  Multiplexer #(.width(5), .enable("false")) multiplexer_15 (
    .in0({5{1'b0}}), .in1(body_entry_2_t), .out(body_entry_2_masked), .sel(bmask[2]));
  Multiplexer #(.width(5), .enable("false")) multiplexer_16 (
    .in0({5{1'b0}}), .in1(body_entry_1_t), .out(body_entry_1_masked), .sel(bmask[1]));
  Multiplexer #(.width(5), .enable("false")) multiplexer_17 (
    .in0({5{1'b0}}), .in1(body_entry_0_t), .out(body_entry_0_masked), .sel(bmask[0]));

  // Other names for the same wires on the sheet: bmask_0 = bmask[0]; bmask_1 = bmask[1]; bmask_2 = bmask[2];
  //   bmask_3 = bmask[3]; bmask_4 = bmask[4]; bmask_5 = bmask[5]; bmask_6 = bmask[6]; bmask_7 = bmask[7];
  //   bmask_8 = bmask[8]; bmask_9 = bmask[9]; bmask_10 = bmask[10]; bmask_11 = bmask[11]; bmask_12 = bmask[12];
  //   bmask_13 = bmask[13]; bmask_14 = bmask[14]; bmask_15 = bmask[15]; q[2:0] = X[7:5]; r[4:0] = X[4:0]; r0 = X[0];
  //   r1 = X[1]; r2 = X[2]; r3 = X[3]; r4 = X[4]
endmodule

module MSR_block (
  input  Din,
  input  op,
  input  CLK,
  input  [4:0] shift_threshold,
  input  [4:0] i,
  input  Q_i_1,
  input  Q_i_1_2,
  output Q_i
);

  wire multiplexer_1_out, multiplexer_2_out, multiplexer_3_out, state_1, state_2, state_3;

  Multiplexer #(.enable("false")) multiplexer_1 (.in0(Din), .in1(Q_i_1), .out(multiplexer_1_out), .sel(state_1));
  Multiplexer #(.enable("false")) multiplexer_2 (
    .in0(multiplexer_1_out), .in1(Q_i), .out(multiplexer_2_out), .sel(state_3));
  Comparator #(.width(5), .mode("unsigned")) comparator_1 (
    .a(shift_threshold), .b(i), .gt(state_1), .eq(state_2), .lt(state_3));
  Multiplexer #(.enable("false")) multiplexer_3 (.in0(multiplexer_2_out), .in1(Q_i), .out(multiplexer_3_out), .sel(op));
  D_Flip_Flop d_ff_1 (.clk(CLK), .D(multiplexer_3_out), .Q(Q_i));  // open: Qn, preset, en, reset

  // Other names for the same wires on the sheet: Q_i_1_t = Q_i_1_2
endmodule

module MSR_24 (
  input  Din,
  input  CLK,
  input  op,
  input  [4:0] shift_threshold,
  output [23:0] contents
);

  // Probe on shift_threshold
  // Probe on shift_threshold
  MSR_block msr_block_1 (
    .Din(Din), .op(op), .shift_threshold(shift_threshold), .i(5'b10111), .Q_i_1(1'b0),
    .Q_i_1_2(contents[22]), .CLK(CLK), .Q_i(contents[23]));
  MSR_block msr_block_2 (
    .Din(Din), .op(op), .shift_threshold(shift_threshold), .i(5'b01111), .Q_i_1(contents[16]),
    .Q_i_1_2(contents[14]), .CLK(CLK), .Q_i(contents[15]));
  MSR_block msr_block_3 (
    .Din(Din), .op(op), .shift_threshold(shift_threshold), .i(5'b00111), .Q_i_1(contents[8]),
    .Q_i_1_2(contents[6]), .CLK(CLK), .Q_i(contents[7]));
  MSR_block msr_block_4 (
    .Din(Din), .op(op), .shift_threshold(shift_threshold), .i(5'b10110), .Q_i_1(contents[23]),
    .Q_i_1_2(contents[21]), .CLK(CLK), .Q_i(contents[22]));
  MSR_block msr_block_5 (
    .Din(Din), .op(op), .shift_threshold(shift_threshold), .i(5'b01110), .Q_i_1(contents[15]),
    .Q_i_1_2(contents[13]), .CLK(CLK), .Q_i(contents[14]));
  MSR_block msr_block_6 (
    .Din(Din), .op(op), .shift_threshold(shift_threshold), .i(5'b00110), .Q_i_1(contents[7]),
    .Q_i_1_2(contents[5]), .CLK(CLK), .Q_i(contents[6]));
  MSR_block msr_block_7 (
    .Din(Din), .op(op), .shift_threshold(shift_threshold), .i(5'b10101), .Q_i_1(contents[22]),
    .Q_i_1_2(contents[20]), .CLK(CLK), .Q_i(contents[21]));
  MSR_block msr_block_8 (
    .Din(Din), .op(op), .shift_threshold(shift_threshold), .i(5'b01101), .Q_i_1(contents[14]),
    .Q_i_1_2(contents[12]), .CLK(CLK), .Q_i(contents[13]));
  MSR_block msr_block_9 (
    .Din(Din), .op(op), .shift_threshold(shift_threshold), .i(5'b00101), .Q_i_1(contents[6]),
    .Q_i_1_2(contents[4]), .CLK(CLK), .Q_i(contents[5]));
  MSR_block msr_block_10 (
    .Din(Din), .op(op), .shift_threshold(shift_threshold), .i(5'b10100), .Q_i_1(contents[21]),
    .Q_i_1_2(contents[19]), .CLK(CLK), .Q_i(contents[20]));
  MSR_block msr_block_11 (
    .Din(Din), .op(op), .shift_threshold(shift_threshold), .i(5'b01100), .Q_i_1(contents[13]),
    .Q_i_1_2(contents[11]), .CLK(CLK), .Q_i(contents[12]));
  MSR_block msr_block_12 (
    .Din(Din), .op(op), .shift_threshold(shift_threshold), .i(5'b00100), .Q_i_1(contents[5]),
    .Q_i_1_2(contents[3]), .CLK(CLK), .Q_i(contents[4]));
  MSR_block msr_block_13 (
    .Din(Din), .op(op), .shift_threshold(shift_threshold), .i(5'b10011), .Q_i_1(contents[20]),
    .Q_i_1_2(contents[18]), .CLK(CLK), .Q_i(contents[19]));
  MSR_block msr_block_14 (
    .Din(Din), .op(op), .shift_threshold(shift_threshold), .i(5'b01011), .Q_i_1(contents[12]),
    .Q_i_1_2(contents[10]), .CLK(CLK), .Q_i(contents[11]));
  MSR_block msr_block_15 (
    .Din(Din), .op(op), .shift_threshold(shift_threshold), .i(5'b00011), .Q_i_1(contents[4]),
    .Q_i_1_2(contents[2]), .CLK(CLK), .Q_i(contents[3]));
  MSR_block msr_block_16 (
    .Din(Din), .op(op), .shift_threshold(shift_threshold), .i(5'b10010), .Q_i_1(contents[19]),
    .Q_i_1_2(contents[17]), .CLK(CLK), .Q_i(contents[18]));
  MSR_block msr_block_17 (
    .Din(Din), .op(op), .shift_threshold(shift_threshold), .i(5'b01010), .Q_i_1(contents[11]),
    .Q_i_1_2(contents[9]), .CLK(CLK), .Q_i(contents[10]));
  MSR_block msr_block_18 (
    .Din(Din), .op(op), .shift_threshold(shift_threshold), .i(5'b00010), .Q_i_1(contents[3]),
    .Q_i_1_2(contents[1]), .CLK(CLK), .Q_i(contents[2]));
  MSR_block msr_block_19 (
    .Din(Din), .op(op), .shift_threshold(shift_threshold), .i(5'b10001), .Q_i_1(contents[18]),
    .Q_i_1_2(contents[16]), .CLK(CLK), .Q_i(contents[17]));
  MSR_block msr_block_20 (
    .Din(Din), .op(op), .shift_threshold(shift_threshold), .i(5'b01001), .Q_i_1(contents[10]),
    .Q_i_1_2(contents[8]), .CLK(CLK), .Q_i(contents[9]));
  MSR_block msr_block_21 (
    .Din(Din), .op(op), .shift_threshold(shift_threshold), .i(5'b00001), .Q_i_1(contents[2]),
    .Q_i_1_2(contents[0]), .CLK(CLK), .Q_i(contents[1]));
  MSR_block msr_block_22 (
    .Din(Din), .op(op), .shift_threshold(shift_threshold), .i(5'b10000), .Q_i_1(contents[17]),
    .Q_i_1_2(contents[15]), .CLK(CLK), .Q_i(contents[16]));
  MSR_block msr_block_23 (
    .Din(Din), .op(op), .shift_threshold(shift_threshold), .i(5'b01000), .Q_i_1(contents[9]),
    .Q_i_1_2(contents[7]), .CLK(CLK), .Q_i(contents[8]));
  MSR_block msr_block_24 (
    .Din(Din), .op(op), .shift_threshold(shift_threshold), .i({5{1'b0}}), .Q_i_1(contents[1]), .CLK(CLK),
    .Q_i(contents[0]));  // open: Q_i_1_2

  // Other names for the same wires on the sheet: contents_0 = contents[0]; contents_1 = contents[1];
  //   contents_2 = contents[2]; contents_3 = contents[3]; contents_4 = contents[4]; contents_5 = contents[5];
  //   contents_6 = contents[6]; contents_7 = contents[7]; contents_8 = contents[8]; contents_9 = contents[9];
  //   contents_10 = contents[10]; contents_11 = contents[11]; contents_12 = contents[12]; contents_13 = contents[13];
  //   contents_14 = contents[14]; contents_15 = contents[15]; contents_16 = contents[16]; contents_17 = contents[17];
  //   contents_18 = contents[18]; contents_19 = contents[19]; contents_20 = contents[20]; contents_21 = contents[21];
  //   contents_22 = contents[22]; contents_23 = contents[23]
endmodule

module ppc_sum_24 (
  input  [23:0] x,
  output [4:0] y_23,
  output [4:0] y_22,
  output [4:0] y_21,
  output [4:0] y_20,
  output [4:0] y_19,
  output [4:0] y_18,
  output [4:0] y_17,
  output [4:0] y_16,
  output [4:0] y_15,
  output [4:0] y_14,
  output [4:0] y_13,
  output [4:0] y_12,
  output [4:0] y_11,
  output [4:0] y_10,
  output [4:0] y_9,
  output [4:0] y_8,
  output [4:0] y_7,
  output [4:0] y_6,
  output [4:0] y_5,
  output [4:0] y_4,
  output [4:0] y_3,
  output [4:0] y_2,
  output [4:0] y_1,
  output [4:0] y_0
);

  wire [4:0] bit_extender_1_out, bit_extender_2_out, bit_extender_3_out, bit_extender_4_out,
       bit_extender_5_out, bit_extender_6_out, bit_extender_7_out, bit_extender_8_out, bit_extender_9_out,
       bit_extender_10_out, bit_extender_11_out, bit_extender_12_out, bit_extender_13_out,
       bit_extender_14_out, bit_extender_15_out, bit_extender_16_out, bit_extender_17_out,
       bit_extender_18_out, bit_extender_19_out, bit_extender_20_out, bit_extender_21_out,
       bit_extender_22_out, bit_extender_23_out, bit_extender_24_out;
  wire [23:0] shifter_1_out;

  // Probe on shifter_1_out
  Shifter #(.width(24), .shift("lr")) shifter_1 (.in(x), .\dist (5'b00001), .out(shifter_1_out));
  assign bit_extender_1_out = {{4{1'b0}}, shifter_1_out[23]};  // Bit_Extender bit_extender_1
  assign bit_extender_2_out = {{4{1'b0}}, shifter_1_out[22]};  // Bit_Extender bit_extender_2
  assign bit_extender_3_out = {{4{1'b0}}, shifter_1_out[21]};  // Bit_Extender bit_extender_3
  assign bit_extender_4_out = {{4{1'b0}}, shifter_1_out[20]};  // Bit_Extender bit_extender_4
  assign bit_extender_5_out = {{4{1'b0}}, shifter_1_out[19]};  // Bit_Extender bit_extender_5
  assign bit_extender_6_out = {{4{1'b0}}, shifter_1_out[18]};  // Bit_Extender bit_extender_6
  assign bit_extender_7_out = {{4{1'b0}}, shifter_1_out[17]};  // Bit_Extender bit_extender_7
  assign bit_extender_8_out = {{4{1'b0}}, shifter_1_out[16]};  // Bit_Extender bit_extender_8
  assign bit_extender_9_out = {{4{1'b0}}, shifter_1_out[15]};  // Bit_Extender bit_extender_9
  assign bit_extender_10_out = {{4{1'b0}}, shifter_1_out[14]};  // Bit_Extender bit_extender_10
  assign bit_extender_11_out = {{4{1'b0}}, shifter_1_out[13]};  // Bit_Extender bit_extender_11
  assign bit_extender_12_out = {{4{1'b0}}, shifter_1_out[12]};  // Bit_Extender bit_extender_12
  assign bit_extender_13_out = {{4{1'b0}}, shifter_1_out[11]};  // Bit_Extender bit_extender_13
  assign bit_extender_14_out = {{4{1'b0}}, shifter_1_out[10]};  // Bit_Extender bit_extender_14
  assign bit_extender_15_out = {{4{1'b0}}, shifter_1_out[9]};  // Bit_Extender bit_extender_15
  assign bit_extender_16_out = {{4{1'b0}}, shifter_1_out[8]};  // Bit_Extender bit_extender_16
  assign bit_extender_17_out = {{4{1'b0}}, shifter_1_out[7]};  // Bit_Extender bit_extender_17
  assign bit_extender_18_out = {{4{1'b0}}, shifter_1_out[6]};  // Bit_Extender bit_extender_18
  assign bit_extender_19_out = {{4{1'b0}}, shifter_1_out[5]};  // Bit_Extender bit_extender_19
  assign bit_extender_20_out = {{4{1'b0}}, shifter_1_out[4]};  // Bit_Extender bit_extender_20
  assign bit_extender_21_out = {{4{1'b0}}, shifter_1_out[3]};  // Bit_Extender bit_extender_21
  assign bit_extender_22_out = {{4{1'b0}}, shifter_1_out[2]};  // Bit_Extender bit_extender_22
  assign bit_extender_23_out = {{4{1'b0}}, shifter_1_out[1]};  // Bit_Extender bit_extender_23
  assign bit_extender_24_out = {{4{1'b0}}, shifter_1_out[0]};  // Bit_Extender bit_extender_24
  Adder #(.width(5)) adder_1 (.a({5{1'b0}}), .b(bit_extender_1_out), .out(y_23));  // open: cin, cout
  Adder #(.width(5)) adder_2 (.a(y_23), .b(bit_extender_2_out), .out(y_22));  // open: cin, cout
  Adder #(.width(5)) adder_3 (.a(y_22), .b(bit_extender_3_out), .out(y_21));  // open: cin, cout
  Adder #(.width(5)) adder_4 (.a(y_21), .b(bit_extender_4_out), .out(y_20));  // open: cin, cout
  Adder #(.width(5)) adder_5 (.a(y_20), .b(bit_extender_5_out), .out(y_19));  // open: cin, cout
  Adder #(.width(5)) adder_6 (.a(y_19), .b(bit_extender_6_out), .out(y_18));  // open: cin, cout
  Adder #(.width(5)) adder_7 (.a(y_18), .b(bit_extender_7_out), .out(y_17));  // open: cin, cout
  Adder #(.width(5)) adder_8 (.a(y_17), .b(bit_extender_8_out), .out(y_16));  // open: cin, cout
  Adder #(.width(5)) adder_9 (.a(y_16), .b(bit_extender_9_out), .out(y_15));  // open: cin, cout
  Adder #(.width(5)) adder_10 (.a(y_15), .b(bit_extender_10_out), .out(y_14));  // open: cin, cout
  Adder #(.width(5)) adder_11 (.a(y_14), .b(bit_extender_11_out), .out(y_13));  // open: cin, cout
  Adder #(.width(5)) adder_12 (.a(y_13), .b(bit_extender_12_out), .out(y_12));  // open: cin, cout
  Adder #(.width(5)) adder_13 (.a(y_12), .b(bit_extender_13_out), .out(y_11));  // open: cin, cout
  Adder #(.width(5)) adder_14 (.a(y_11), .b(bit_extender_14_out), .out(y_10));  // open: cin, cout
  Adder #(.width(5)) adder_15 (.a(y_10), .b(bit_extender_15_out), .out(y_9));  // open: cin, cout
  Adder #(.width(5)) adder_16 (.a(y_9), .b(bit_extender_16_out), .out(y_8));  // open: cin, cout
  Adder #(.width(5)) adder_17 (.a(y_8), .b(bit_extender_17_out), .out(y_7));  // open: cin, cout
  Adder #(.width(5)) adder_18 (.a(y_7), .b(bit_extender_18_out), .out(y_6));  // open: cin, cout
  Adder #(.width(5)) adder_19 (.a(y_6), .b(bit_extender_19_out), .out(y_5));  // open: cin, cout
  Adder #(.width(5)) adder_20 (.a(y_5), .b(bit_extender_20_out), .out(y_4));  // open: cin, cout
  Adder #(.width(5)) adder_21 (.a(y_4), .b(bit_extender_21_out), .out(y_3));  // open: cin, cout
  Adder #(.width(5)) adder_22 (.a(y_3), .b(bit_extender_22_out), .out(y_2));  // open: cin, cout
  Adder #(.width(5)) adder_23 (.a(y_2), .b(bit_extender_23_out), .out(y_1));  // open: cin, cout
  Adder #(.width(5)) adder_24 (.a(y_1), .b(bit_extender_24_out), .out(y_0));  // open: cin, cout
endmodule

module MSR_16 (
  input  Din,
  input  CLK,
  input  op,
  input  [4:0] shift_threshold,
  output [15:0] contents
);

  // Probe on shift_threshold
  MSR_block msr_block_1 (
    .Din(Din), .op(op), .shift_threshold(shift_threshold), .i(5'b01111), .Q_i_1(1'b0),
    .Q_i_1_2(contents[14]), .CLK(CLK), .Q_i(contents[15]));
  MSR_block msr_block_2 (
    .Din(Din), .op(op), .shift_threshold(shift_threshold), .i(5'b00111), .Q_i_1(contents[8]),
    .Q_i_1_2(contents[6]), .CLK(CLK), .Q_i(contents[7]));
  MSR_block msr_block_3 (
    .Din(Din), .op(op), .shift_threshold(shift_threshold), .i(5'b01110), .Q_i_1(contents[15]),
    .Q_i_1_2(contents[13]), .CLK(CLK), .Q_i(contents[14]));
  MSR_block msr_block_4 (
    .Din(Din), .op(op), .shift_threshold(shift_threshold), .i(5'b00110), .Q_i_1(contents[7]),
    .Q_i_1_2(contents[5]), .CLK(CLK), .Q_i(contents[6]));
  MSR_block msr_block_5 (
    .Din(Din), .op(op), .shift_threshold(shift_threshold), .i(5'b01101), .Q_i_1(contents[14]),
    .Q_i_1_2(contents[12]), .CLK(CLK), .Q_i(contents[13]));
  MSR_block msr_block_6 (
    .Din(Din), .op(op), .shift_threshold(shift_threshold), .i(5'b00101), .Q_i_1(contents[6]),
    .Q_i_1_2(contents[4]), .CLK(CLK), .Q_i(contents[5]));
  MSR_block msr_block_7 (
    .Din(Din), .op(op), .shift_threshold(shift_threshold), .i(5'b01100), .Q_i_1(contents[13]),
    .Q_i_1_2(contents[11]), .CLK(CLK), .Q_i(contents[12]));
  MSR_block msr_block_8 (
    .Din(Din), .op(op), .shift_threshold(shift_threshold), .i(5'b00100), .Q_i_1(contents[5]),
    .Q_i_1_2(contents[3]), .CLK(CLK), .Q_i(contents[4]));
  MSR_block msr_block_9 (
    .Din(Din), .op(op), .shift_threshold(shift_threshold), .i(5'b01011), .Q_i_1(contents[12]),
    .Q_i_1_2(contents[10]), .CLK(CLK), .Q_i(contents[11]));
  MSR_block msr_block_10 (
    .Din(Din), .op(op), .shift_threshold(shift_threshold), .i(5'b00011), .Q_i_1(contents[4]),
    .Q_i_1_2(contents[2]), .CLK(CLK), .Q_i(contents[3]));
  MSR_block msr_block_11 (
    .Din(Din), .op(op), .shift_threshold(shift_threshold), .i(5'b01010), .Q_i_1(contents[11]),
    .Q_i_1_2(contents[9]), .CLK(CLK), .Q_i(contents[10]));
  MSR_block msr_block_12 (
    .Din(Din), .op(op), .shift_threshold(shift_threshold), .i(5'b00010), .Q_i_1(contents[3]),
    .Q_i_1_2(contents[1]), .CLK(CLK), .Q_i(contents[2]));
  MSR_block msr_block_13 (
    .Din(Din), .op(op), .shift_threshold(shift_threshold), .i(5'b01001), .Q_i_1(contents[10]),
    .Q_i_1_2(contents[8]), .CLK(CLK), .Q_i(contents[9]));
  MSR_block msr_block_14 (
    .Din(Din), .op(op), .shift_threshold(shift_threshold), .i(5'b00001), .Q_i_1(contents[2]),
    .Q_i_1_2(contents[0]), .CLK(CLK), .Q_i(contents[1]));
  MSR_block msr_block_15 (
    .Din(Din), .op(op), .shift_threshold(shift_threshold), .i(5'b01000), .Q_i_1(contents[9]),
    .Q_i_1_2(contents[7]), .CLK(CLK), .Q_i(contents[8]));
  MSR_block msr_block_16 (
    .Din(Din), .op(op), .shift_threshold(shift_threshold), .i({5{1'b0}}), .Q_i_1(contents[1]), .CLK(CLK),
    .Q_i(contents[0]));  // open: Q_i_1_2

  // Other names for the same wires on the sheet: contents_0 = contents[0]; contents_1 = contents[1];
  //   contents_2 = contents[2]; contents_3 = contents[3]; contents_4 = contents[4]; contents_5 = contents[5];
  //   contents_6 = contents[6]; contents_7 = contents[7]; contents_8 = contents[8]; contents_9 = contents[9];
  //   contents_10 = contents[10]; contents_11 = contents[11]; contents_12 = contents[12]; contents_13 = contents[13];
  //   contents_14 = contents[14]; contents_15 = contents[15]
endmodule

module transpose_16_5 (
  input  [15:0] x0,
  input  [15:0] x1,
  input  [15:0] x2,
  input  [15:0] x3,
  input  [15:0] x4,
  output [4:0] y15,
  output [4:0] y14,
  output [4:0] y13,
  output [4:0] y12,
  output [4:0] y11,
  output [4:0] y10,
  output [4:0] y9,
  output [4:0] y8,
  output [4:0] y7,
  output [4:0] y6,
  output [4:0] y5,
  output [4:0] y4,
  output [4:0] y3,
  output [4:0] y2,
  output [4:0] y1,
  output [4:0] y0
);

  BitSelector #(.width(16)) bitselector_1 (.in(x0), .out(y0[0]), .sel(4'b0000));
  BitSelector #(.width(16)) bitselector_2 (.in(x1), .out(y0[1]), .sel(4'b0000));
  BitSelector #(.width(16)) bitselector_3 (.in(x2), .out(y0[2]), .sel(4'b0000));
  BitSelector #(.width(16)) bitselector_4 (.in(x3), .out(y0[3]), .sel(4'b0000));
  BitSelector #(.width(16)) bitselector_5 (.in(x4), .out(y0[4]), .sel(4'b0000));
  BitSelector #(.width(16)) bitselector_6 (.in(x0), .out(y4[0]), .sel(4'b0100));
  BitSelector #(.width(16)) bitselector_7 (.in(x1), .out(y4[1]), .sel(4'b0100));
  BitSelector #(.width(16)) bitselector_8 (.in(x2), .out(y4[2]), .sel(4'b0100));
  BitSelector #(.width(16)) bitselector_9 (.in(x3), .out(y4[3]), .sel(4'b0100));
  BitSelector #(.width(16)) bitselector_10 (.in(x4), .out(y4[4]), .sel(4'b0100));
  BitSelector #(.width(16)) bitselector_11 (.in(x0), .out(y8[0]), .sel(4'b1000));
  BitSelector #(.width(16)) bitselector_12 (.in(x1), .out(y8[1]), .sel(4'b1000));
  BitSelector #(.width(16)) bitselector_13 (.in(x2), .out(y8[2]), .sel(4'b1000));
  BitSelector #(.width(16)) bitselector_14 (.in(x3), .out(y8[3]), .sel(4'b1000));
  BitSelector #(.width(16)) bitselector_15 (.in(x4), .out(y8[4]), .sel(4'b1000));
  BitSelector #(.width(16)) bitselector_16 (.in(x0), .out(y12[0]), .sel(4'b1100));
  BitSelector #(.width(16)) bitselector_17 (.in(x1), .out(y12[1]), .sel(4'b1100));
  BitSelector #(.width(16)) bitselector_18 (.in(x2), .out(y12[2]), .sel(4'b1100));
  BitSelector #(.width(16)) bitselector_19 (.in(x3), .out(y12[3]), .sel(4'b1100));
  BitSelector #(.width(16)) bitselector_20 (.in(x4), .out(y12[4]), .sel(4'b1100));
  BitSelector #(.width(16)) bitselector_21 (.in(x0), .out(y1[0]), .sel(4'b0001));
  BitSelector #(.width(16)) bitselector_22 (.in(x1), .out(y1[1]), .sel(4'b0001));
  BitSelector #(.width(16)) bitselector_23 (.in(x2), .out(y1[2]), .sel(4'b0001));
  BitSelector #(.width(16)) bitselector_24 (.in(x3), .out(y1[3]), .sel(4'b0001));
  BitSelector #(.width(16)) bitselector_25 (.in(x4), .out(y1[4]), .sel(4'b0001));
  BitSelector #(.width(16)) bitselector_26 (.in(x0), .out(y5[0]), .sel(4'b0101));
  BitSelector #(.width(16)) bitselector_27 (.in(x1), .out(y5[1]), .sel(4'b0101));
  BitSelector #(.width(16)) bitselector_28 (.in(x2), .out(y5[2]), .sel(4'b0101));
  BitSelector #(.width(16)) bitselector_29 (.in(x3), .out(y5[3]), .sel(4'b0101));
  BitSelector #(.width(16)) bitselector_30 (.in(x4), .out(y5[4]), .sel(4'b0101));
  BitSelector #(.width(16)) bitselector_31 (.in(x0), .out(y9[0]), .sel(4'b1001));
  BitSelector #(.width(16)) bitselector_32 (.in(x1), .out(y9[1]), .sel(4'b1001));
  BitSelector #(.width(16)) bitselector_33 (.in(x2), .out(y9[2]), .sel(4'b1001));
  BitSelector #(.width(16)) bitselector_34 (.in(x3), .out(y9[3]), .sel(4'b1001));
  BitSelector #(.width(16)) bitselector_35 (.in(x4), .out(y9[4]), .sel(4'b1001));
  BitSelector #(.width(16)) bitselector_36 (.in(x0), .out(y13[0]), .sel(4'b1101));
  BitSelector #(.width(16)) bitselector_37 (.in(x1), .out(y13[1]), .sel(4'b1101));
  BitSelector #(.width(16)) bitselector_38 (.in(x2), .out(y13[2]), .sel(4'b1101));
  BitSelector #(.width(16)) bitselector_39 (.in(x3), .out(y13[3]), .sel(4'b1101));
  BitSelector #(.width(16)) bitselector_40 (.in(x4), .out(y13[4]), .sel(4'b1101));
  BitSelector #(.width(16)) bitselector_41 (.in(x0), .out(y2[0]), .sel(4'b0010));
  BitSelector #(.width(16)) bitselector_42 (.in(x1), .out(y2[1]), .sel(4'b0010));
  BitSelector #(.width(16)) bitselector_43 (.in(x2), .out(y2[2]), .sel(4'b0010));
  BitSelector #(.width(16)) bitselector_44 (.in(x3), .out(y2[3]), .sel(4'b0010));
  BitSelector #(.width(16)) bitselector_45 (.in(x4), .out(y2[4]), .sel(4'b0010));
  BitSelector #(.width(16)) bitselector_46 (.in(x0), .out(y6[0]), .sel(4'b0110));
  BitSelector #(.width(16)) bitselector_47 (.in(x1), .out(y6[1]), .sel(4'b0110));
  BitSelector #(.width(16)) bitselector_48 (.in(x2), .out(y6[2]), .sel(4'b0110));
  BitSelector #(.width(16)) bitselector_49 (.in(x3), .out(y6[3]), .sel(4'b0110));
  BitSelector #(.width(16)) bitselector_50 (.in(x4), .out(y6[4]), .sel(4'b0110));
  BitSelector #(.width(16)) bitselector_51 (.in(x0), .out(y10[0]), .sel(4'b1010));
  BitSelector #(.width(16)) bitselector_52 (.in(x1), .out(y10[1]), .sel(4'b1010));
  BitSelector #(.width(16)) bitselector_53 (.in(x2), .out(y10[2]), .sel(4'b1010));
  BitSelector #(.width(16)) bitselector_54 (.in(x3), .out(y10[3]), .sel(4'b1010));
  BitSelector #(.width(16)) bitselector_55 (.in(x4), .out(y10[4]), .sel(4'b1010));
  BitSelector #(.width(16)) bitselector_56 (.in(x0), .out(y14[0]), .sel(4'b1110));
  BitSelector #(.width(16)) bitselector_57 (.in(x1), .out(y14[1]), .sel(4'b1110));
  BitSelector #(.width(16)) bitselector_58 (.in(x2), .out(y14[2]), .sel(4'b1110));
  BitSelector #(.width(16)) bitselector_59 (.in(x3), .out(y14[3]), .sel(4'b1110));
  BitSelector #(.width(16)) bitselector_60 (.in(x4), .out(y14[4]), .sel(4'b1110));
  BitSelector #(.width(16)) bitselector_61 (.in(x0), .out(y3[0]), .sel(4'b0011));
  BitSelector #(.width(16)) bitselector_62 (.in(x1), .out(y3[1]), .sel(4'b0011));
  BitSelector #(.width(16)) bitselector_63 (.in(x2), .out(y3[2]), .sel(4'b0011));
  BitSelector #(.width(16)) bitselector_64 (.in(x3), .out(y3[3]), .sel(4'b0011));
  BitSelector #(.width(16)) bitselector_65 (.in(x4), .out(y3[4]), .sel(4'b0011));
  BitSelector #(.width(16)) bitselector_66 (.in(x0), .out(y7[0]), .sel(4'b0111));
  BitSelector #(.width(16)) bitselector_67 (.in(x1), .out(y7[1]), .sel(4'b0111));
  BitSelector #(.width(16)) bitselector_68 (.in(x2), .out(y7[2]), .sel(4'b0111));
  BitSelector #(.width(16)) bitselector_69 (.in(x3), .out(y7[3]), .sel(4'b0111));
  BitSelector #(.width(16)) bitselector_70 (.in(x4), .out(y7[4]), .sel(4'b0111));
  BitSelector #(.width(16)) bitselector_71 (.in(x0), .out(y11[0]), .sel(4'b1011));
  BitSelector #(.width(16)) bitselector_72 (.in(x1), .out(y11[1]), .sel(4'b1011));
  BitSelector #(.width(16)) bitselector_73 (.in(x2), .out(y11[2]), .sel(4'b1011));
  BitSelector #(.width(16)) bitselector_74 (.in(x3), .out(y11[3]), .sel(4'b1011));
  BitSelector #(.width(16)) bitselector_75 (.in(x4), .out(y11[4]), .sel(4'b1011));
  BitSelector #(.width(16)) bitselector_76 (.in(x0), .out(y15[0]), .sel(4'b1111));
  BitSelector #(.width(16)) bitselector_77 (.in(x1), .out(y15[1]), .sel(4'b1111));
  BitSelector #(.width(16)) bitselector_78 (.in(x2), .out(y15[2]), .sel(4'b1111));
  BitSelector #(.width(16)) bitselector_79 (.in(x3), .out(y15[3]), .sel(4'b1111));
  BitSelector #(.width(16)) bitselector_80 (.in(x4), .out(y15[4]), .sel(4'b1111));
endmodule
